// Digital circuit circuito casa.dig as structural Verilog
module circuito_casa (
  input  P,
  input  F1,
  input  F2,
  input  L,
  output C1,
  output C2,
  output CE,
  output B,
  output SL,
  output SRE
);

  wire and_2_out, and_3_out, not_1_out, not_2_out;

  not not_1 (not_1_out, P);
  not not_2 (not_2_out, F1);
  and and_1 (C1, not_2_out, F2, not_1_out);
  and and_2 (and_2_out, F1, not_1_out);
  and and_3 (and_3_out, F2, not_1_out);
  or or_1 (CE, and_2_out, and_3_out);

  assign B = F2;
  assign C2 = P;
  assign SL = L;
  assign SRE = F1;
endmodule
